// Logisim project 2bit_signed_arithmetic_unit.circ as structural Verilog: 1 circuit, main circuit main
module main (
  input  in_1,
  input  A1,
  input  A0,
  input  B1,
  input  B0,
  input  Cin0,
  input  Zero,
  input  Cin2,
  input  [1:0] sel,
  output S0,
  output S1,
  output A,
  output ADD_OVE,
  output B,
  output D0,
  output C,
  output D1,
  output D,
  output SUB_OVE,
  output SIG,
  output P0,
  output P1,
  output P2,
  output P3
);

  wire adder_1_cout, adder_2_cout, adder_3_cout, adder_4_cout, and_2_out, and_3_out, and_4_out, and_5_out,
       not_1_out, not_2_out;

  not not_1 (not_1_out, B1);
  not not_2 (not_2_out, B0);
  Adder #(.width(1)) adder_1 (.a(A0), .b(B0), .out(S0), .cin(Cin0), .cout(adder_1_cout));
  Adder #(.width(1)) adder_2 (.a(A1), .b(B1), .out(S1), .cin(adder_1_cout), .cout(adder_2_cout));
  Adder #(.width(1)) adder_3 (.a(A0), .b(not_2_out), .out(D0), .cin(Cin2), .cout(adder_3_cout));
  Adder #(.width(1)) adder_4 (.a(A1), .b(not_1_out), .out(D1), .cin(adder_3_cout), .cout(adder_4_cout));
  and and_1 (P0, A0, B0);
  and and_2 (and_2_out, A0, B1);
  and and_3 (and_3_out, A1, B0);
  and and_4 (and_4_out, A1, B1);
  xor xor_1 (ADD_OVE, adder_1_cout, adder_2_cout);
  LED add_overflow (.in(ADD_OVE));
  xor xor_2 (SUB_OVE, adder_3_cout, adder_4_cout);
  LED sub_overflow (.in(SUB_OVE));
  LED sign (.in(D1));
  xor xor_3 (P1, and_2_out, and_3_out);
  and and_5 (and_5_out, and_2_out, and_3_out);
  xor xor_4 (P2, and_5_out, and_4_out);
  and and_6 (P3, and_5_out, and_4_out);
  Multiplexer #(.select(2)) multiplexer_1 (.in0(Zero), .in1(S0), .in2(D0), .in3(P0), .out(A), .sel(sel));
  Multiplexer #(.select(2)) multiplexer_2 (.in0(Zero), .in1(S1), .in2(D1), .in3(P1), .out(B), .sel(sel));
  Multiplexer #(.select(2)) multiplexer_3 (.in0(Zero), .in1(adder_2_cout), .in2(Zero), .in3(P2), .out(C), .sel(sel));
  Multiplexer #(.select(2)) multiplexer_4 (.in0(Zero), .in1(Zero), .in2(Zero), .in3(P3), .out(D), .sel(sel));

  assign SIG = D1;
endmodule
